// Logisim project cpu8bit.circ as structural Verilog: 5 circuits, main circuit main
module main (
  input  Reset
);

  wire ALUSrc, and_1_out, Branch, Jump, MemRead, MemToReg, MemWrite, not_1_out, or_1_out, Pulso_out, RegDst,
       RegWrite, ula_1_igual;
  wire [1:0] ALUOp;
  wire [2:0] controle_ula_1_ulactrl, multiplexer_2_out, opcode, rs, rt;
  wire [2:2] rd;
  wire [7:0] adder_1_out, address_imm, banco_de_registradores_1_read_data_1, contRT, Memoria_RAM_dout,
       multiplexer_1_out, multiplexer_3_out, multiplexer_4_out, PC_q, ula_1_r;

  Clock Pulso (.out(Pulso_out));
  Register PC (.D(multiplexer_1_out), .Q(PC_q), .clk(Pulso_out), .clr(Reset));  // open: en
  Adder adder_1 (.a(8'h1), .b(PC_q), .out(adder_1_out));  // open: cin, cout
  ROM #(.dataWidth(18)) Memoria (.addr(PC_q), .data({opcode, rs, rt, rd[2], address_imm}));
  Multiplexer #(.width(8)) multiplexer_1 (
    .in0(adder_1_out), .in1(address_imm), .out(multiplexer_1_out), .sel(or_1_out));
  or or_1 (or_1_out, Jump, and_1_out);
  Multiplexer #(.width(3)) multiplexer_2 (
    .in0(rt), .in1({rd[2], address_imm[7:6]}), .out(multiplexer_2_out), .sel(RegDst));
  Unidade_Controle unidade_controle_1 (
    .opcode(opcode), .RegDst(RegDst), .RegWrite(RegWrite), .ALUSrc(ALUSrc), .MemWrite(MemWrite),
    .MemRead(MemRead), .MemToReg(MemToReg), .Branch(Branch), .Jump(Jump), .ALUOp(ALUOp));
  Banco_de_registradores banco_de_registradores_1 (
    .Read_register_1(rs), .Read_register_2(rt), .Write_data(multiplexer_4_out),
    .Write_register(multiplexer_2_out), .RegWrite(RegWrite), .Clock(Pulso_out), .Reset(Reset),
    .Read_data_1(banco_de_registradores_1_read_data_1), .Read_data_2(contRT));
  Multiplexer #(.width(8)) multiplexer_3 (.in0(contRT), .in1(address_imm), .out(multiplexer_3_out), .sel(ALUSrc));
  Controle_ULA controle_ula_1 (.Funct(address_imm[2:0]), .ALUOp(ALUOp), .ULACtrl(controle_ula_1_ulactrl));
  ULA ula_1 (
    .A(banco_de_registradores_1_read_data_1), .B(multiplexer_3_out), .Funcao(controle_ula_1_ulactrl),
    .Shamt(address_imm[5:3]), .R(ula_1_r), .Igual(ula_1_igual));
  and and_1 (and_1_out, Branch, ula_1_igual);
  not not_1 (not_1_out, Pulso_out);
  RAM Memoria_RAM (.addr(ula_1_r), .we(MemWrite), .oe(MemRead), .clk(not_1_out), .din(contRT), .dout(Memoria_RAM_dout));
  Multiplexer #(.width(8)) multiplexer_4 (
    .in0(Memoria_RAM_dout), .in1(ula_1_r), .out(multiplexer_4_out), .sel(MemToReg));

  // Other names for the same wires on the sheet: funct[2:0] = address_imm[2:0]; rd[1:0] = address_imm[7:6];
  //   shamnt[2:0] = address_imm[5:3]

  // Notes on the sheet:
  //   contents of Memoria (hex, n*v repeats v):
  //   20205 10201 20403 10402 20602 10603 8201 8402 14c0 8803 3940 10a05 38009
endmodule

module Banco_de_registradores (
  input  [2:0] Read_register_1,
  input  [2:0] Read_register_2,
  input  [7:0] Write_data,
  input  [2:0] Write_register,
  input  RegWrite,
  input  Clock,
  input  Reset,
  output [7:0] Read_data_1,
  output [7:0] Read_data_2
);

  wire WE0, WE1, WE2, WE3, WE4, WE5, WE6, WE7;
  wire [7:0] demultiplexer_2_out0, demultiplexer_2_out1, demultiplexer_2_out2, demultiplexer_2_out3,
       demultiplexer_2_out4, demultiplexer_2_out5, demultiplexer_2_out6, demultiplexer_2_out7, Reg0, Reg1,
       Reg2, Reg3, Reg4, Reg5, Reg6, Reg7;

  Demultiplexer #(.select(3)) demultiplexer_1 (
    .out0(WE0), .out1(WE1), .out2(WE2), .out3(WE3), .out4(WE4), .out5(WE5), .out6(WE6), .out7(WE7),
    .in(RegWrite), .sel(Write_register));
  Demultiplexer #(.select(3), .width(8)) demultiplexer_2 (
    .out0(demultiplexer_2_out0), .out1(demultiplexer_2_out1), .out2(demultiplexer_2_out2),
    .out3(demultiplexer_2_out3), .out4(demultiplexer_2_out4), .out5(demultiplexer_2_out5),
    .out6(demultiplexer_2_out6), .out7(demultiplexer_2_out7), .in(Write_data), .sel(Write_register));
  Register u_Reg0 (.D(demultiplexer_2_out0), .en(WE0), .Q(Reg0), .clk(Clock), .clr(Reset));
  Register u_Reg1 (.D(demultiplexer_2_out1), .en(WE1), .Q(Reg1), .clk(Clock), .clr(Reset));
  Register u_Reg2 (.D(demultiplexer_2_out2), .en(WE2), .Q(Reg2), .clk(Clock), .clr(Reset));
  Register u_Reg3 (.D(demultiplexer_2_out3), .en(WE3), .Q(Reg3), .clk(Clock), .clr(Reset));
  Register u_Reg4 (.D(demultiplexer_2_out4), .en(WE4), .Q(Reg4), .clk(Clock), .clr(Reset));
  Register u_Reg5 (.D(demultiplexer_2_out5), .en(WE5), .Q(Reg5), .clk(Clock), .clr(Reset));
  Register u_Reg6 (.D(demultiplexer_2_out6), .en(WE6), .Q(Reg6), .clk(Clock), .clr(Reset));
  Register u_Reg7 (.D(demultiplexer_2_out7), .en(WE7), .Q(Reg7), .clk(Clock), .clr(Reset));
  Multiplexer #(.select(3), .width(8)) multiplexer_1 (
    .in0(Reg0), .in1(Reg1), .in2(Reg2), .in3(Reg3), .in4(Reg4), .in5(Reg5), .in6(Reg6), .in7(Reg7),
    .out(Read_data_1), .sel(Read_register_1));
  Multiplexer #(.select(3), .width(8)) multiplexer_2 (
    .in0(Reg0), .in1(Reg1), .in2(Reg2), .in3(Reg3), .in4(Reg4), .in5(Reg5), .in6(Reg6), .in7(Reg7),
    .out(Read_data_2), .sel(Read_register_2));

  // Other names for the same wires on the sheet: Read1[2:0] = Read_register_1; Read2[2:0] = Read_register_2
endmodule

module ULA (
  input  [7:0] A,
  input  [7:0] B,
  input  [2:0] Funcao,
  input  [2:0] Shamt,
  output [7:0] R,
  output Igual
);

  wire comparator_1_lt;
  wire [7:0] AComp, adder_1_out, ADiv, AMulti, ANeg, AShiftDir, AShiftEsq, ASoma, ASub, BComp, BDiv,
       bit_extender_1_out, BMulti, BNeg, BSoma, BSub, divider_1_out, multiplier_1_out, negator_1_out,
       shifter_1_out, shifter_2_out, subtractor_1_out;

  Demultiplexer #(.select(3), .width(8)) demultiplexer_1 (
    .out0(ASoma), .out1(ASub), .out2(AMulti), .out3(ADiv), .out4(ANeg), .out5(AComp), .out6(AShiftEsq),
    .out7(AShiftDir), .in(A), .sel(Funcao));
  Demultiplexer #(.select(3), .width(8)) demultiplexer_2 (
    .out0(BSoma), .out1(BSub), .out2(BMulti), .out3(BDiv), .out4(BNeg), .out5(BComp), .in(B), .sel(Funcao));  // open: out6, out7
  Adder adder_1 (.a(ASoma), .b(BSoma), .out(adder_1_out));  // open: cin, cout
  Subtractor subtractor_1 (.a(ASub), .b(BSub), .out(subtractor_1_out));  // open: bin, bout
  Multiplier multiplier_1 (.a(AMulti), .b(BMulti), .out(multiplier_1_out));  // open: cin, cout
  Divider divider_1 (.a(ADiv), .b(BDiv), .out(divider_1_out));  // open: upper, rem
  Negator negator_1 (.in(ANeg), .out(negator_1_out));
  Comparator comparator_1 (.a(AComp), .b(BComp), .eq(Igual), .lt(comparator_1_lt));  // open: gt
  Shifter shifter_1 (.in(AShiftEsq), .\dist (Shamt), .out(shifter_1_out));
  Shifter #(.shift("lr")) shifter_2 (.in(AShiftDir), .\dist (Shamt), .out(shifter_2_out));
  assign bit_extender_1_out = {{7{1'b0}}, comparator_1_lt};  // Bit_Extender bit_extender_1
  Multiplexer #(.select(3), .width(8)) multiplexer_1 (
    .in0(adder_1_out), .in1(subtractor_1_out), .in2(multiplier_1_out), .in3(divider_1_out),
    .in4(negator_1_out), .in5(bit_extender_1_out), .in6(shifter_1_out), .in7(shifter_2_out), .out(R),
    .sel(Funcao));
endmodule

module Unidade_Controle (
  input  [2:0] opcode,
  output RegDst,
  output RegWrite,
  output ALUSrc,
  output MemWrite,
  output MemRead,
  output MemToReg,
  output Branch,
  output Jump,
  output [1:0] ALUOp
);

  wire and_1_out, and_2_out, and_3_out, and_6_out, and_7_out, nor_2_out, not_1_out, not_2_out, not_3_out,
       not_4_out, not_5_out, not_6_out, not_7_out, not_8_out, not_9_out, not_10_out, not_11_out, not_12_out,
       not_13_out, not_14_out, not_15_out, not_16_out, not_17_out;

  not not_1 (not_1_out, opcode[0]);
  not not_2 (not_2_out, opcode[1]);
  and and_1 (and_1_out, not_1_out, not_2_out, opcode[2]);
  not not_3 (not_3_out, opcode[0]);
  not not_4 (not_4_out, opcode[2]);
  not not_5 (not_5_out, opcode[1]);
  not not_6 (not_6_out, opcode[2]);
  not not_7 (not_7_out, opcode[0]);
  not not_8 (not_8_out, opcode[1]);
  not not_9 (not_9_out, opcode[2]);
  not not_10 (not_10_out, opcode[0]);
  not not_11 (not_11_out, opcode[1]);
  not not_12 (not_12_out, opcode[2]);
  and and_2 (and_2_out, opcode[0], opcode[1], not_13_out);
  not not_13 (not_13_out, opcode[2]);
  not not_14 (not_14_out, opcode[0]);
  not not_15 (not_15_out, opcode[1]);
  and and_3 (and_3_out, not_14_out, not_15_out, opcode[2]);
  not not_16 (not_16_out, opcode[0]);
  not not_17 (not_17_out, opcode[1]);
  nor nor_1 (RegDst, opcode[0], opcode[1], opcode[2]);
  nor nor_2 (nor_2_out, opcode[1], opcode[2]);
  or or_1 (RegWrite, nor_2_out, and_1_out);
  ExactlyOne xor_1 (.out(ALUSrc), .in0(opcode[0]), .in1(opcode[1]), .in2(opcode[2]));
  and and_4 (MemWrite, not_3_out, opcode[1], not_4_out);
  and and_5 (MemRead, opcode[0], not_5_out, not_6_out);
  and and_6 (and_6_out, not_7_out, not_8_out, not_9_out);
  or or_2 (MemToReg, and_6_out, and_7_out);
  and and_7 (and_7_out, not_10_out, not_11_out, opcode[2]);
  and and_8 (Branch, opcode[0], opcode[1], not_12_out);
  and and_9 (Jump, opcode[0], opcode[1], opcode[2]);
  or or_3 (ALUOp[0], and_2_out, and_3_out);
  and and_10 (ALUOp[1], not_16_out, not_17_out);
endmodule

module Controle_ULA (
  input  [2:0] Funct,
  input  [1:0] ALUOp,
  output [2:0] ULACtrl
);

  Multiplexer #(.select(2), .width(3)) multiplexer_1 (
    .in0(3'b000), .in1(3'b101), .in2(Funct), .in3(3'b000), .out(ULACtrl), .sel(ALUOp));
endmodule
